// Digital circuit 6502.toy.logics.v2.dig as structural Verilog
module _6502_toy_logics_v2 (
  input  A8,
  input  A9,
  input  A10,
  input  A11,
  input  A12,
  input  A13,
  input  A14,
  input  A15,
  input  irq01,
  input  irq2,
  input  irq3,
  input  irq4,
  input  irq5,
  input  irq6,
  input  XTAL1,
  input  in_21,
  input  A4,
  input  A5,
  input  A6,
  input  _1_8432_MHz,
  input  in_40,
  input  in_41,
  input  in_42,
  input  in_43,
  input  phi2,
  input  r_w,
  input  A7,
  output dev,
  output rom,
  output CS_RAM,
  output CS_ROM,
  output CS_DEV,
  output XTAL2,
  output XTAL,
  output CS_IRQ,
  output BANKS,
  output CIA,
  output VIA1,
  output VIA2,
  output EXT0,
  output EXT1,
  output EXT2,
  output EXT3,
  output PHI0,
  output out_38,
  output out_39,
  output CS_OE,
  output CS_WE,
  output EXT4,
  output UR0,
  output UR1,
  output UR2,
  output UR3,
  output UR4,
  output UR5,
  output UR6,
  output UR7
);

  wire _7400_1_pin6, _7404_1_pin2, _7404_1_pin3, _7404_1_pin4, _7404_1_pin5, _7404_1_pin6, _7404_1_pin9,
       _7474_1_pin2, pullup_4_out;

  PullUp pullup_1 (.out(irq01));
  PullUp pullup_2 (.out(irq2));
  PullUp pullup_3 (.out(irq3));
  PullUp pullup_4 (.out(pullup_4_out));
  _7474 _7474_1 (
    .pin1(pullup_4_out), .pin2(_7474_1_pin2), .pin3(XTAL), .pin4(pullup_4_out), .pin5(PHI0),
    .pin6(_7474_1_pin2), .pin7(1'b0), .pin8(out_38), .pin9(out_39), .pin10(in_40), .pin11(in_42),
    .pin12(in_43), .pin13(in_40), .pin14(1'b1));
  _7404 _7404_1 (
    .pin1(A8), .pin2(_7404_1_pin2), .pin3(_7404_1_pin3), .pin4(_7404_1_pin4), .pin5(_7404_1_pin5),
    .pin6(_7404_1_pin6), .pin7(1'b0), .pin8(CS_IRQ), .pin9(_7404_1_pin9), .pin10(XTAL), .pin11(in_21),
    .pin12(XTAL2), .pin13(XTAL1), .pin14(1'b1));
  _7430 _7430_1 (
    .pin1(_7404_1_pin2), .pin2(A9), .pin3(A10), .pin4(A11), .pin5(A12), .pin6(A13), .pin7(1'b0), .pin8(dev),
    .pin11(A14), .pin12(A15), .pin14(1'b1));  // open: pin9, pin10, pin13
  _7410 _7410_1 (
    .pin1(A15), .pin2(A14), .pin3(irq01), .pin4(irq2), .pin5(irq3), .pin6(_7404_1_pin5), .pin7(1'b0),
    .pin8(_7404_1_pin3), .pin9(irq4), .pin10(irq5), .pin11(irq6), .pin12(rom), .pin13(A13), .pin14(1'b1));
  PullUp pullup_5 (.out(in_40));
  PullUp pullup_6 (.out(irq5));
  PullUp pullup_7 (.out(irq6));
  PullUp pullup_8 (.out(irq4));
  _7400 _7400_1 (
    .pin1(rom), .pin2(rom), .pin3(CS_RAM), .pin4(dev), .pin5(dev), .pin6(_7400_1_pin6), .pin7(1'b0),
    .pin8(CS_ROM), .pin9(dev), .pin10(CS_RAM), .pin11(CS_DEV), .pin12(_7400_1_pin6), .pin13(CS_RAM),
    .pin14(1'b1));
  _7400 _7400_2 (
    .pin1(_7404_1_pin6), .pin2(_7404_1_pin4), .pin3(_7404_1_pin9), .pin4(1'b0), .pin5(1'b0), .pin6(EXT4),
    .pin7(1'b0), .pin8(CS_WE), .pin9(CS_OE), .pin10(phi2), .pin11(CS_OE), .pin12(r_w), .pin13(phi2));  // open: pin14
  PullUp pullup_9 (.out(CS_IRQ));
  PullUp pullup_10 (.out(CS_DEV));
  PullUp pullup_11 (.out(CS_ROM));
  PullUp pullup_12 (.out(CS_RAM));
  _74138 _74138_1 (
    .pin1(A4), .pin2(A5), .pin3(A6), .pin4(A7), .pin5(CS_DEV), .pin6(1'b1), .pin7(EXT3), .pin9(EXT2),
    .pin10(EXT1), .pin11(EXT0), .pin12(VIA2), .pin13(VIA1), .pin14(CIA), .pin15(BANKS), .pin16(1'b1));  // open: pin8
  _74138 _74138_2 (
    .pin1(A4), .pin2(A5), .pin3(A6), .pin4(CS_DEV), .pin5(1'b0), .pin6(A7), .pin7(UR7), .pin8(1'b0),
    .pin9(UR6), .pin10(UR5), .pin11(UR4), .pin12(UR3), .pin13(UR2), .pin14(UR1), .pin15(UR0), .pin16(1'b1));

  assign in_41 = in_40;
endmodule
