// Digital circuit 65C02.toy.chips.dig as structural Verilog
module _65C02_toy_chips (
  output out_1
);

  // _7400 _7400_1: pin names not known; wires that end beside it: 1'b1
  // _7410 _7410_1: pin names not known; wires that end beside it: 1'b0
  // _28c64 _28c64_1: pin names not known; wires that end beside it: out_1
endmodule
