// Digital circuit 65C02.toy.logics.dig as structural Verilog
module _65C02_toy_logics (
  input  PHI2,
  input  R_W,
  input  A15,
  input  A14,
  input  A13,
  input  HA_2,
  input  HB,
  input  A8,
  input  A9,
  input  A10,
  input  A11,
  input  A12,
  input  HA_3,
  input  IRQ0,
  input  IRQ1,
  input  IRQ2,
  input  IRQ3,
  input  IRQ4,
  input  IRQ5,
  output HA,
  output RAM,
  output DEV,
  output ROM,
  output WR,
  output RD,
  output HB_2,
  output IRQ
);

  wire nand_2_out, nand_3_out, nand_6_out, or_1_out, or_2_out, or_3_out, or_4_out, or_5_out;

  nand nand_1 (HA, A15, A14, A13);
  nand nand_2 (nand_2_out, IRQ0, IRQ1, IRQ2);
  nand nand_3 (nand_3_out, IRQ3, IRQ4, IRQ5);
  nand nand_4 (RD, PHI2, R_W);
  nand nand_5 (RAM, HA_2, HA_2);
  nand nand_6 (nand_6_out, HB, HB);
  or or_1 (or_1_out, HA_3, A12);
  or or_2 (or_2_out, A8, A9);
  or or_3 (or_3_out, A10, A11);
  or or_4 (or_4_out, or_2_out, or_3_out);
  or or_5 (or_5_out, nand_2_out, nand_3_out);
  nand nand_7 (WR, PHI2, RD);
  nand nand_8 (ROM, RAM, HB);
  nand nand_9 (DEV, RAM, nand_6_out);
  or or_6 (HB_2, or_1_out, or_4_out);
  nand nand_10 (IRQ, or_5_out, or_5_out);

  // Notes on the sheet:
  //   65C02.TOY, minimal SBC
  //   SRAM = HM62256    32k x 8
  //   EEPROM = AT28C64 8k x 8
  //   Devices = W65C22S x 2, NM6551 x 1
  //   CPU = W65C02S
  //   Memory Map:
  //   $0000 - $DFFF,	SRAM ~ 56kb 
  //   $E000 - $E0FF,	Devices 16 x 16 bytes
  //   $E100 - $FFFF,	EEPROM ~ 8kb
  //   SIgnals:
  //   A15 a A8,    Address
  //   PHI2, R/W, ENABLE, States
  //   /WR, /RW, /RAM, /ROM, /DEV, Controls
  //   PS: ENABLE could be VDD (5V)
endmodule
