// Digital circuit glue-logics.dig as structural Verilog
module glue_logics (
  input  A15,
  input  A14,
  input  A13,
  input  A12,
  input  R_W,
  input  PHI2,
  input  A8,
  input  A9,
  input  A10,
  input  A11,
  output CSRAM,
  output OE,
  output CSDEV,
  output WE,
  output CSROM,
  output DVC0,
  output DVC1,
  output DVC2,
  output DVC3,
  output DVC4,
  output DVC5,
  output DVC6,
  output DVC7,
  output NC,
  output NC_2
);

  wire _74139_1_pin5, _74139_1_pin6, _74139_1_pin7, and_1_out, nand_1_out;

  nand nand_1 (nand_1_out, A15, A14);
  _74139 _74139_1 (
    .pin1(nand_1_out), .pin2(A13), .pin3(A12), .pin4(CSDEV), .pin5(_74139_1_pin5), .pin6(_74139_1_pin6),
    .pin7(_74139_1_pin7), .pin8(1'b0), .pin9(OE), .pin10(WE), .pin11(NC_2), .pin12(NC), .pin13(PHI2),
    .pin14(R_W), .pin15(1'b0), .pin16(1'b1));
  and and_1 (and_1_out, _74139_1_pin7, _74139_1_pin6);
  and and_2 (CSROM, and_1_out, _74139_1_pin5);
  nand nand_2 (CSRAM, nand_1_out, nand_1_out);
  _74138 _74138_1 (
    .pin1(A8), .pin2(A9), .pin3(A10), .pin4(CSDEV), .pin5(CSDEV), .pin6(A11), .pin7(DVC7), .pin8(1'b0),
    .pin9(DVC6), .pin10(DVC5), .pin11(DVC4), .pin12(DVC3), .pin13(DVC2), .pin14(DVC1), .pin15(DVC0),
    .pin16(1'b1));
endmodule
