// Digital circuit test0.dig as structural Verilog
module test0 (
  input  ROM,
  input  DEV,
  input  in_6,
  input  in_7,
  input  in_8,
  input  in_10,
  input  in_11,
  input  in_12,
  output CS_RAM,
  output CS_DEV,
  output CS_ROM,
  output out_9,
  output out_13,
  output out_14,
  output out_15,
  output out_16,
  output out_17,
  output out_18
);

  wire nand_2_out, nand_5_out, nand_9_out, not_1_out, not_2_out, or_1_out;

  nand nand_1 (CS_RAM, ROM, ROM);
  nand nand_2 (nand_2_out, DEV, DEV);
  nand nand_3 (out_9, in_6, in_7, in_8);
  nand nand_4 (out_13, in_10, in_11, in_12);
  nand nand_5 (nand_5_out, in_6, in_7, in_8, in_6, in_10, in_11, in_12, in_10);
  and and_1 (out_18, in_6, in_7, in_8, in_6, in_10, in_11, in_11, in_10);
  nand nand_6 (CS_ROM, DEV, CS_RAM);
  nand nand_7 (CS_DEV, nand_2_out, CS_RAM);
  not not_1 (not_1_out, out_9);
  not not_2 (not_2_out, out_13);
  nand nand_8 (out_14, out_9, out_13);
  nand nand_9 (nand_9_out, not_1_out, not_2_out);
  not not_3 (out_16, nand_5_out);
  or or_1 (or_1_out, out_13, out_9);
  not not_4 (out_17, nand_9_out);
  not not_5 (out_15, or_1_out);
endmodule
