// Digital circuit 65C02.toy.circuit.dig as structural Verilog
module _65C02_toy_circuit (
  input  A4,
  input  A5,
  input  A6,
  input  A7,
  input  A0,
  input  A1,
  input  A2,
  input  A3,
  input  ENABLE,
  input  PHI2,
  input  R_W,
  input  A15,
  input  A13,
  input  A14,
  input  A11,
  input  A10,
  input  A9,
  input  A8,
  input  A12,
  output DVC0,
  output DVC1,
  output DVC2,
  output DVC3,
  output DVC4,
  output DVC5,
  output DVC6,
  output DVC7__BANKS,
  output bank0,
  output bank1,
  output bank2,
  output bank3,
  output bank4,
  output bank5,
  output bank6,
  output bank7,
  output WR,
  output RD,
  output DEV,
  output RAM,
  output ROM
);

  wire _7410_1_pin8, _7432_1_pin3, _7432_1_pin6, _7432_1_pin8, _7432_2_pin3;

  _7410 _7410_1 (
    .pin1(PHI2), .pin2(R_W), .pin3(PHI2), .pin4(RD), .pin5(ENABLE), .pin6(WR), .pin7(1'b0),
    .pin8(_7410_1_pin8), .pin9(A15), .pin10(A14), .pin11(A13), .pin12(RD), .pin13(ENABLE), .pin14(1'b1));
  _7432 _7432_1 (
    .pin1(A11), .pin2(A10), .pin3(_7432_1_pin3), .pin4(A9), .pin5(A8), .pin6(_7432_1_pin6), .pin7(1'b0),
    .pin8(_7432_1_pin8), .pin9(_7432_1_pin6), .pin10(_7432_1_pin3), .pin11(1'b1), .pin12(1'b1), .pin13(1'b1),
    .pin14(1'b1));
  _7432 _7432_2 (
    .pin1(_7410_1_pin8), .pin2(A12), .pin3(_7432_2_pin3), .pin4(_7432_2_pin3), .pin5(_7432_1_pin8),
    .pin6(DEV), .pin7(1'b0), .pin8(1'b1), .pin9(1'b1), .pin10(1'b1), .pin11(1'b1), .pin12(1'b1),
    .pin13(1'b1), .pin14(1'b1));
  _7400 _7400_1 (
    .pin1(_7410_1_pin8), .pin2(_7410_1_pin8), .pin3(RAM), .pin4(RAM), .pin5(DEV), .pin6(ROM), .pin7(1'b0),
    .pin8(1'b0), .pin9(1'b1), .pin10(1'b1), .pin11(1'b0), .pin12(1'b1), .pin13(1'b1), .pin14(1'b1));
  _74138 _74138_1 (
    .pin1(A4), .pin2(A5), .pin3(A6), .pin4(DEV), .pin5(DEV), .pin6(A7), .pin7(DVC7__BANKS), .pin8(1'b0),
    .pin9(DVC6), .pin10(DVC5), .pin11(DVC4), .pin12(DVC3), .pin13(DVC2), .pin14(DVC1), .pin15(DVC0),
    .pin16(1'b1));
  LED led_1 (.in(ROM));
  LED led_2 (.in(RAM));
  LED led_3 (.in(DEV));
  LED led_4 (.in(DVC0));
  LED led_5 (.in(DVC1));
  LED led_6 (.in(DVC2));
  LED led_7 (.in(DVC3));
  LED led_8 (.in(DVC4));
  LED led_9 (.in(DVC5));
  LED led_10 (.in(DVC6));
  LED led_11 (.in(DVC7__BANKS));
  _74138 _74138_2 (
    .pin1(A0), .pin2(A1), .pin3(A2), .pin4(DVC0), .pin5(DVC0), .pin6(A3), .pin7(bank7), .pin8(1'b0),
    .pin9(bank6), .pin10(bank5), .pin11(bank4), .pin12(bank3), .pin13(bank2), .pin14(bank1), .pin15(bank0),
    .pin16(1'b1));
  LED led_12 (.in(bank0));
  LED led_13 (.in(bank1));
  LED led_14 (.in(bank2));
  LED led_15 (.in(bank3));
  LED led_16 (.in(bank4));
  LED led_17 (.in(bank5));
  LED led_18 (.in(bank6));
  LED led_19 (.in(bank7));

  // Notes on the sheet:
  //   65C02.TOY, minimal SBC
  //   SRAM = HM62256    32k x 8
  //   EEPROM = AT28C64 8k x 8
  //   Devices = W65C22S x 2, NM6551 x 1
  //   CPU = W65C02S
  //   Memory Map:
  //   $0000 - $DFFF,	SRAM ~ 56kb 
  //   $E000 - $E0FF,	Devices 16 x 16 bytes
  //   $E100 - $FFFF,	EEPROM ~ 8kb
  //   SIgnals:
  //   A15 a A8,    Address
  //   PHI2, R/W, ENABLE, States
  //   /WR, /RW, /RAM, /ROM, /DEV, Controls
  //   PS: ENABLE could be VDD (5V)
endmodule
