// Digital circuit 65C02.toy.logics.dig as structural Verilog
module _65C02_toy_logics (
  input  PHI2,
  input  R_W,
  input  ENABLE,
  input  A15,
  input  A14,
  input  A13,
  input  HA_2,
  input  DEV,
  input  A8,
  input  A9,
  input  A10,
  input  A11,
  input  A12,
  input  HA_3,
  output HA,
  output CE__RAM,
  output CE__DEV,
  output CE__ROM,
  output WR,
  output RD,
  output DEV_2
);

  wire nand_3_out, or_1_out, or_2_out, or_3_out, or_4_out;

  nand nand_1 (RD, PHI2, R_W, ENABLE);
  nand nand_2 (CE__RAM, HA_2, HA_2);
  nand nand_3 (nand_3_out, DEV, DEV);
  nand nand_4 (HA, A15, A14, A13);
  or or_1 (or_1_out, HA_3, A12);
  or or_2 (or_2_out, A8, A9);
  or or_3 (or_3_out, A10, A11);
  or or_4 (or_4_out, or_2_out, or_3_out);
  nand nand_5 (WR, PHI2, RD, ENABLE);
  nand nand_6 (CE__ROM, CE__RAM, DEV);
  nand nand_7 (CE__DEV, CE__RAM, nand_3_out);
  or or_5 (DEV_2, or_1_out, or_4_out);

  // Notes on the sheet:
  //   74HC10 - NAND-3 x 3
  //   74HC00 - NAND-2 x 4
  //   65C02.TOY, minimal SBC
  //   SRAM = HM62256    32k x 8
  //   EEPROM = AT28C64 8k x 8
  //   Devices = W65C22S x 2, NM6551 x 1
  //   CPU = W65C02S
  //   Memory Map:
  //   $0000 - $DFFF,	SRAM ~ 56kb 
  //   $E000 - $E0FF,	Devices 16 x 16 bytes
  //   $E100 - $FFFF,	EEPROM ~ 8kb
  //   SIgnals:
  //   A15 a A8,    Address
  //   PHI2, R/W, ENABLE, States
  //   /WR, /RW, /RAM, /ROM, /DEV, Controls
  //   PS: ENABLE could be VDD (5V)
endmodule
