// Digital circuit decoder.dig as structural Verilog
module decoder (
  input  A15,
  input  phi2,
  input  R_W,
  input  A14,
  input  A13,
  input  A12,
  input  A11,
  input  in_15,
  output CSRAM,
  output CSDEV,
  output CSROM,
  output OE,
  output WE,
  output out_13,
  output out_14
);

  wire nand_1_out, nand_2_out, nand_4_out, or_1_out;

  nand nand_1 (nand_1_out, A15, A14);
  nand nand_2 (nand_2_out, A13, A12);
  or or_1 (or_1_out, nand_1_out, nand_2_out);
  nand nand_3 (out_14, out_13, in_15);
  nand nand_4 (nand_4_out, A11, A11);
  nand nand_5 (OE, phi2, R_W);
  nand nand_6 (WE, OE, phi2);
  nand nand_7 (out_13, phi2, out_14);
  nand nand_8 (CSRAM, or_1_out, or_1_out);
  or or_2 (CSDEV, or_1_out, A11);
  or or_3 (CSROM, or_1_out, nand_4_out);
endmodule
