// Digital circuit glue-decoder.dig as structural Verilog
module glue_decoder (
  input  A15,
  input  A14,
  input  A13,
  input  A12,
  input  R_W,
  input  PHI2,
  input  A8,
  input  A9,
  input  A10,
  input  A11,
  input  A17,
  input  A16,
  input  R_W_2,
  input  PHI3,
  input  A19,
  input  A18,
  output CSRAM,
  output OE,
  output CSDEV,
  output WE,
  output CSROM,
  output DVC0,
  output DVC1,
  output DVC2,
  output DVC3,
  output DVC4,
  output DVC5,
  output DVC6,
  output DVC7,
  output CSRAM_2,
  output OE_2,
  output WE_2
);

  wire _7400_1_pin3, _7400_1_pin11, _7400_1_pin12, _7400_2_pin6, nand_1_out, nand_2_out, nand_3_out, or_1_out;

  _7400 _7400_1 (
    .pin1(A17), .pin2(A16), .pin3(_7400_1_pin3), .pin4(_7400_1_pin3), .pin5(_7400_1_pin3), .pin6(CSRAM_2),
    .pin11(_7400_1_pin11), .pin12(_7400_1_pin12), .pin13(_7400_1_pin12));  // open: pin7, pin8, pin9, pin10, pin14
  _7432 _7432_1 (
    .pin1(_7400_1_pin3), .pin2(_7400_1_pin11), .pin11(_7400_1_pin12), .pin12(A18), .pin13(A19));  // open: pin3, pin4, pin5, pin6, pin7, pin8, pin9, pin10, pin14
  _7400 _7400_2 (
    .pin1(PHI3), .pin2(R_W_2), .pin3(OE_2), .pin4(R_W_2), .pin5(R_W_2), .pin6(_7400_2_pin6), .pin11(WE_2),
    .pin12(_7400_2_pin6), .pin13(PHI3));  // open: pin7, pin8, pin9, pin10, pin14
  nand nand_1 (nand_1_out, A15, A14);
  or or_1 (or_1_out, A13, A12);
  nand nand_2 (nand_2_out, R_W, R_W);
  _74138 _74138_1 (
    .pin1(A8), .pin2(A9), .pin3(A10), .pin4(1'b0), .pin5(1'b0), .pin6(A11), .pin7(DVC7), .pin8(1'b0),
    .pin9(DVC6), .pin10(DVC5), .pin11(DVC4), .pin12(DVC3), .pin13(DVC2), .pin14(DVC1), .pin15(DVC0),
    .pin16(1'b1));
  nand nand_3 (nand_3_out, or_1_out, or_1_out);
  nand nand_4 (OE, PHI2, R_W);
  nand nand_5 (WE, PHI2, nand_2_out);
  nand nand_6 (CSRAM, nand_1_out, nand_1_out);
  or or_2 (CSDEV, or_1_out, nand_1_out);
  or or_3 (CSROM, nand_3_out, nand_1_out);
endmodule
